# Fritzing sketch arduino_led (saved by Fritzing 0.9.3b)
circuit board: 6.88566cm x 5.36311cm
breadboards: 1

parts:
  LED2 = LED - 5mm [color="Red (633nm)" package="5 mm [THT]"]
  Arduino2 = Arduino Uno (Rev3)
  R5 = Resistor [tolerance=±5% resistance=330 package=THT]

nets:
  N1: LED2.cathode, Arduino2.GND
  N2: LED2.anode, R5.Pin_0
  N3: Arduino2.D13/SCK, R5.Pin_1
