# Fritzing sketch arduino_potentiometer (saved by Fritzing 0.9.3b)
circuit board: 6.88566cm x 5.36311cm
breadboards: 1

parts:
  R1 = Rotary Potentiometer (Small) [maximum_resistance=100kΩ package=THT]
  Arduino2 = Arduino Uno (Rev3)

nets (from the breadboard view):
  N1: R1.leg1, Arduino2.GND
  N2: R1.wiper, Arduino2.A0
  N3: R1.leg2, Arduino2.5V
